// Digital circuit assignment1SBass.dig as structural Verilog
module assignment1SBass (
  input  A,
  input  B,
  input  A_2,
  input  B_2,
  input  A_3,
  input  B_3,
  output C,
  output D,
  output E,
  output Q,
  output C_2,
  output Q_2,
  output R
);

  wire not_1_out;

  and and_1 (E, A, B);
  not not_1 (not_1_out, A_3);
  xor xor_1 (Q_2, A_3, B_3);
  not not_2 (C, A);
  xor xor_2 (D, A, B);
  xor xor_3 (Q, A_2, B_2);
  and and_2 (C_2, A_2, B_2);
  and and_3 (R, not_1_out, B_3);
endmodule
